# Fritzing sketch schema_RFID_acces_locaux (saved by Fritzing 0.9.3b)
breadboards: 1

parts:
  Raspberry_Pi_1 = Raspberry Pi 3 [part_number=RPI-3-V1.2]
  Composant1 = RFID-RC522-v2
  LED1 = LED - 5mm [color="Red (633nm)" package="5 mm [THT]"]
  LED2 = LED - 5mm [color="Red (633nm)" package="5 mm [THT]"]
  LCD1 = LCD screen

nets:
  3V3: Raspberry_Pi_1.3v3, Composant1.3.3V, LED1.anode, LED2.anode, LCD1.VDD, LCD1.LED+
  N1: Raspberry_Pi_1.GIPO4, LCD1.DB7
  N2: Raspberry_Pi_1.GIPO17, LCD1.DB5
  N3: Raspberry_Pi_1.GIPO10, Composant1.MOSI
  N4: Raspberry_Pi_1.GIPO9, Composant1.MISO
  N5: Raspberry_Pi_1.GIPO11, Composant1.SCK
  N6: Raspberry_Pi_1.GIPO8, Composant1.SDA
  N7: Raspberry_Pi_1.GIPO25, Composant1.RST, LCD1.RS
  GND: Raspberry_Pi_1.GND, Composant1.GND, LED1.cathode, LED2.cathode, LCD1.VSS, LCD1.R/W, LCD1.E, LCD1.LED-
  N8: Raspberry_Pi_1.GIPO18, LCD1.DB6
  N9: Raspberry_Pi_1.GIPO14, LCD1.DB4

custom parts:
  RFID-RC522-v2: A simple China made RFID-RC522 Reader; do check the pin labels, as this is a MFRC522 based clone.
